// Logisim project hw4.circ as structural Verilog: 12 circuits, main circuit Main
module Main (
  input  reset
);

  wire _0, _0000, _0001, _1, _2, _3, _4, _5, _6, _7, _8, _9, _0010, _10, _0011, _11, _0100, _0101, _0110,
       _0111, _1000, _1001, _1010, _1011, _1100, _1101, _1110, _1111, add, addi, alu_1_blt, alu_1_bne,
       ALUinB, blt, blt_out, bne, bne_out, BR, BRimm, clk, DMwe, \input , j, J_Type, jal, JP, jr,
       keyboard_1_avail, lw, \not , not_1_out, not_2_out, \output , Rdst, Rwd, Rwe, sll, srl, sub, sw, \xor ;
  wire [2:0] ALUop, multiplexer_4_out, multiplexer_5_out, rd, rs, rt, shamt;
  wire [5:0] Imm;
  wire [6:0] keyboard_1_data;
  wire [7:0] KBD;
  wire [11:0] Address;
  wire [15:0] alu_1_outputdata, BRdest, JPdest, multiplexer_1_out, multiplexer_6_out, multiplexer_7_out,
       multiplexer_8_out, multiplexer_10_out, PC, PC_1, PC_prime, PCIn, plus_BRimm_result, ram_1_data, RD1,
       RD2, WD;
  wire [15:12] Ins;

  Clock u_clk (.out(clk));
  Decoder #(.select(4), .enable("false")) decoder_1 (
    .out0(add), .out1(sub), .out2(\not ), .out3(\xor ), .out4(sll), .out5(srl), .out6(addi), .out7(lw),
    .out8(sw), .out9(bne), .out10(blt), .out11(j), .out12(jr), .out13(jal), .out14(\input ),
    .out15(\output ), .sel(Ins));
  _16_Bit_Ripple_Adder plus_1 (.A(PC_prime), .sub(1'b0), .B(16'h1), .result(PC_1));  // open: ovf
  Register u_PC (.Input(PCIn), .Clk(clk), .WriteEnable(1'b1), .Reset(reset), .out_5(PC));
  Multiplexer #(.width(16), .enable("false")) multiplexer_1 (
    .in0(PC_1), .in1(plus_BRimm_result), .out(multiplexer_1_out), .sel(BRimm));
  _16_Bit_Ripple_Adder plus_BRimm (.A(PC_1), .sub(1'b0), .B(BRdest), .result(plus_BRimm_result));  // open: ovf
  ROM #(.addrWidth(16), .dataWidth(16)) rom_1 (
    .addr(PC), .data({Ins, _11, _10, _9, _8, _7, _6, _5, _4, _3, _2, _1, _0}));  // open: sel
  Decoder #(.select(4), .enable("false")) decoder_2 (
    .out0(_0000), .out1(_0001), .out2(_0010), .out3(_0011), .out4(_0100), .out5(_0101), .out6(_0110),
    .out7(_0111), .out8(_1000), .out9(_1001), .out10(_1010), .out11(_1011), .out12(_1100), .out13(_1101),
    .out14(_1110), .out15(_1111), .sel(Ins));
  Multiplexer #(.width(16), .enable("false")) multiplexer_2 (
    .in0(multiplexer_1_out), .in1(JPdest), .out(PCIn), .sel(JP));
  Instruction_Decode u_Ins (
    .rs(rs), .Instruction({Ins, _11, _10, _9, _8, _7, _6, _5, _4, _3, _2, _1, _0}), .rt(rt), .shamt(shamt),
    .Immediate(Imm), .Address(Address), .rd(rd));
  or OR (J_Type, _1011, _1101);
  Multiplexer #(.width(16), .enable("false")) multiplexer_3 (.in0(PC), .in1(RD1), .out(PC_prime), .sel(jr));
  not not_1 (not_1_out, clk);
  Multiplexer #(.width(3), .enable("false")) multiplexer_4 (
    .in0(multiplexer_5_out), .in1(3'b111), .out(multiplexer_4_out), .sel(jal));
  Multiplexer #(.width(3), .enable("false")) multiplexer_5 (.in0(rd), .in1(rt), .out(multiplexer_5_out), .sel(Rdst));
  RegisterFile registerfile_1 (
    .reset(reset), .ReadReg1(rs), .clk(not_1_out), .ReadReg2(rt), .WriteReg(multiplexer_4_out),
    .WriteData(WD), .RegWriteEnable(Rwe), .ReadData1(RD1), .ReadData2(RD2));
  _6_16_Sign_Extender _6_16_SX (.Input(Imm), .out(BRdest));
  TTY #(.rows(13), .cols(80), .trigger("falling")) tty_1 (.data(RD1[6:0]), .clk(clk), .we(\output ), .clr(reset));
  Control_Decode Control (
    .Instruction({Ins, _11, _10, _9, _8, _7, _6, _5, _4, _3, _2, _1, _0}), .BR(BR), .Rdst(Rdst), .JP(JP),
    .Rwd(Rwd), .ALUinB(ALUinB), .ALUop(ALUop), .DMwe(DMwe), .Rwe(Rwe));
  Multiplexer #(.width(16), .enable("false")) multiplexer_6 (
    .in0(RD2), .in1(multiplexer_7_out), .out(multiplexer_6_out), .sel(ALUinB));
  Multiplexer #(.width(16), .enable("false")) multiplexer_7 (
    .in0(BRdest), .in1(JPdest), .out(multiplexer_7_out), .sel(J_Type));
  _12_16_Sign_Extender _12_16_SX (.Input(Address), .out(JPdest));
  and u_bne (bne_out, alu_1_bne, bne);
  ALU alu_1 (
    .OpType(ALUop), .shamt(shamt), .InputData1(RD1), .InputData2(multiplexer_6_out),
    .OutputData(alu_1_outputdata), .bne(alu_1_bne), .blt(alu_1_blt));
  or or_2 (BRimm, bne_out, blt_out);
  and u_blt (blt_out, alu_1_blt, blt);
  Keyboard keyboard_1 (.clk(clk), .re(\input ), .clr(reset), .avail(keyboard_1_avail), .data(keyboard_1_data));
  not not_2 (not_2_out, clk);
  RAM #(.addrWidth(16), .dataWidth(16), .bus("separate")) ram_1 (
    .addr(alu_1_outputdata), .din(RD2), .data(ram_1_data), .str(DMwe), .clk(not_2_out));  // open: sel, ld, clr
  not not_3 (KBD[7], keyboard_1_avail);
  Multiplexer #(.width(16), .enable("false")) multiplexer_8 (
    .in0(alu_1_outputdata), .in1(ram_1_data), .out(multiplexer_8_out), .sel(Rwd));
  Multiplexer #(.width(7), .enable("false")) multiplexer_9 (
    .in0(keyboard_1_data), .in1({7{1'b0}}), .out(KBD[6:0]), .sel(KBD[7]));
  Multiplexer #(.width(16), .enable("false")) multiplexer_10 (
    .in0(multiplexer_8_out), .in1({{8{1'b0}}, KBD}), .out(multiplexer_10_out), .sel(\input ));
  Multiplexer #(.width(16), .enable("false")) multiplexer_11 (
    .in0(multiplexer_10_out), .in1(PC_1), .out(WD), .sel(jal));

  // Other names for the same wires on the sheet: Ins[11:0] = {_11, _10, _9, _8, _7, _6, _5, _4, _3, _2, _1, _0};
  //   opcode[3:0] = Ins

  // Notes on the sheet:
  //   Instruction Memory (ROM)
  //   contents of rom_1 (hex, n*v repeats v):
  //   6100 6903 e040 62a0 f400 693f 983b 91ff 6fc1 91ff
  //   jr controls
  //   Data Memory (RAM)
  //   Keyboard
  //   TTY
endmodule

module ALU (
  input  [2:0] OpType,
  input  [2:0] shamt,
  input  [15:0] InputData1,
  input  [15:0] InputData2,
  output [15:0] OutputData,
  output bne,
  output blt
);

  wire [15:0] _0, _1, _2, _3, _4, _5;

  _16_Bit_Ripple_Adder add (.A(InputData1), .sub(1'b0), .B(InputData2), .result(_0));  // open: ovf
  _16_Bit_Ripple_Adder sub (.A(InputData1), .sub(1'b1), .B(InputData2), .result(_1));  // open: ovf
  assign _2 = ~InputData1;  // NOT_Gate not, 16 bits wide
  assign _3 = InputData1 ^ InputData2;  // XOR_Gate xor, 16 bits wide
  Left_Shifter sll (.shamt(shamt), .\input (InputData1), .\output (_4));
  Right_Shifter srl (.shamt(shamt), .\input (InputData1), .\output (_5));
  Multiplexer #(.select(3), .width(16), .enable("false")) multiplexer_1 (
    .in0(_0), .in1(_1), .in2(_2), .in3(_3), .in4(_4), .in5(_5), .out(OutputData), .sel(OpType));  // open: in6, in7
  or or_1 (bne, OutputData[0], OutputData[1], OutputData[2], OutputData[3], OutputData[4], OutputData[5], OutputData[6], OutputData[7], OutputData[8], OutputData[9], OutputData[10], OutputData[11], OutputData[12], OutputData[13], OutputData[14], OutputData[15]);
  and and_1 (blt, bne, OutputData[15]);

  // Other names for the same wires on the sheet: In1[15:0] = InputData1; In2[15:0] = InputData2; OT[2:0] = OpType
endmodule

module Instruction_Decode (
  input  [15:0] Instruction,
  output [2:0] rs,
  output [2:0] rt,
  output [2:0] rd,
  output [2:0] shamt,
  output [5:0] Immediate,
  output [11:0] Address
);

  wire _0000, _0001, _0010, _0011, _0100, _0101, _0110, _0111, _1000, _1001, _1010, _1011, _1100, _1101,
       _1110, _1111;

  Decoder #(.select(4), .enable("false")) decoder_1 (
    .out0(_0000), .out1(_0001), .out2(_0010), .out3(_0011), .out4(_0100), .out5(_0101), .out6(_0110),
    .out7(_0111), .out8(_1000), .out9(_1001), .out10(_1010), .out11(_1011), .out12(_1100), .out13(_1101),
    .out14(_1110), .out15(_1111), .sel(Instruction[15:12]));

  assign Address = Instruction[11:0];
  assign Immediate = Instruction[5:0];
  assign rd = Instruction[5:3];
  assign rs = Instruction[11:9];
  assign rt = Instruction[8:6];
  assign shamt = Instruction[2:0];

  // Other names for the same wires on the sheet: _0 = Instruction[0]; _1 = Instruction[1]; _2 = Instruction[2];
  //   _3 = Instruction[3]; _4 = Instruction[4]; _5 = Instruction[5]; opcode[3:0] = Instruction[15:12];
  //   _9 = Instruction[9]; _10 = Instruction[10]; _11 = Instruction[11]; _6 = Instruction[6]; _7 = Instruction[7];
  //   _8 = Instruction[8]
endmodule

module Control_Decode (
  input  [15:0] Instruction,
  output BR,
  output Rdst,
  output JP,
  output Rwd,
  output ALUinB,
  output [2:0] ALUop,
  output DMwe,
  output Rwe
);

  wire add, addi, blt, bne, \input , j, jal, jr, lw, \not , \output , sll, srl, sub, \xor ;

  Decoder #(.select(4), .enable("false")) decoder_1 (
    .out0(add), .out1(sub), .out2(\not ), .out3(\xor ), .out4(sll), .out5(srl), .out6(addi), .out7(lw),
    .out8(DMwe), .out9(bne), .out10(blt), .out11(j), .out12(jr), .out13(jal), .out14(\input ),
    .out15(\output ), .sel(Instruction[15:12]));
  or or_1 (BR, bne, blt);
  or or_2 (JP, j, jal);
  or or_3 (ALUinB, addi, lw, DMwe);
  or or_4 (Rwe, add, sub, \not , \xor , sll, srl, addi, lw, jal, \input );
  or or_5 (Rdst, addi, \input , lw);
  or or_6 (Rwd, lw, \input );
  or or_7 (ALUop[0], sub, \xor , srl, bne, blt);
  or or_8 (ALUop[1], \not , \xor );
  or or_9 (ALUop[2], sll, srl);

  // Other names for the same wires on the sheet: xx1 = ALUop[0]; x1x = ALUop[1]; _1xx = ALUop[2]; _0 = Instruction[0];
  //   _1 = Instruction[1]; _2 = Instruction[2]; _3 = Instruction[3]; _4 = Instruction[4]; _5 = Instruction[5];
  //   _6 = Instruction[6]; _7 = Instruction[7]; _8 = Instruction[8]; _9 = Instruction[9]; _10 = Instruction[10];
  //   _11 = Instruction[11]; opcode[3:0] = Instruction[15:12]; sw = DMwe
endmodule

module Register (
  input  [15:0] Input,
  input  Clk,
  input  WriteEnable,
  input  Reset,
  output [15:0] out_5
);

  D_Flip_Flop d_ff_1 (.clk(Clk), .D(Input[0]), .Q(out_5[0]), .en(WriteEnable), .reset(Reset));  // open: Qn, preset
  D_Flip_Flop d_ff_2 (.clk(Clk), .D(Input[1]), .Q(out_5[1]), .en(WriteEnable), .reset(Reset));  // open: Qn, preset
  D_Flip_Flop d_ff_3 (.clk(Clk), .D(Input[2]), .Q(out_5[2]), .en(WriteEnable), .reset(Reset));  // open: Qn, preset
  D_Flip_Flop d_ff_4 (.clk(Clk), .D(Input[3]), .Q(out_5[3]), .en(WriteEnable), .reset(Reset));  // open: Qn, preset
  D_Flip_Flop d_ff_5 (.clk(Clk), .D(Input[4]), .Q(out_5[4]), .en(WriteEnable), .reset(Reset));  // open: Qn, preset
  D_Flip_Flop d_ff_6 (.clk(Clk), .D(Input[5]), .Q(out_5[5]), .en(WriteEnable), .reset(Reset));  // open: Qn, preset
  D_Flip_Flop d_ff_7 (.clk(Clk), .D(Input[6]), .Q(out_5[6]), .en(WriteEnable), .reset(Reset));  // open: Qn, preset
  D_Flip_Flop d_ff_8 (.clk(Clk), .D(Input[7]), .Q(out_5[7]), .en(WriteEnable), .reset(Reset));  // open: Qn, preset
  D_Flip_Flop d_ff_9 (.clk(Clk), .D(Input[8]), .Q(out_5[8]), .en(WriteEnable), .reset(Reset));  // open: Qn, preset
  D_Flip_Flop d_ff_10 (.clk(Clk), .D(Input[9]), .Q(out_5[9]), .en(WriteEnable), .reset(Reset));  // open: Qn, preset
  D_Flip_Flop d_ff_11 (.clk(Clk), .D(Input[10]), .Q(out_5[10]), .en(WriteEnable), .reset(Reset));  // open: Qn, preset
  D_Flip_Flop d_ff_12 (.clk(Clk), .D(Input[11]), .Q(out_5[11]), .en(WriteEnable), .reset(Reset));  // open: Qn, preset
  D_Flip_Flop d_ff_13 (.clk(Clk), .D(Input[12]), .Q(out_5[12]), .en(WriteEnable), .reset(Reset));  // open: Qn, preset
  D_Flip_Flop d_ff_14 (.clk(Clk), .D(Input[13]), .Q(out_5[13]), .en(WriteEnable), .reset(Reset));  // open: Qn, preset
  D_Flip_Flop d_ff_15 (.clk(Clk), .D(Input[14]), .Q(out_5[14]), .en(WriteEnable), .reset(Reset));  // open: Qn, preset
  D_Flip_Flop d_ff_16 (.clk(Clk), .D(Input[15]), .Q(out_5[15]), .en(WriteEnable), .reset(Reset));  // open: Qn, preset

  // Other names for the same wires on the sheet: D0 = Input[0]; D1 = Input[1]; D2 = Input[2]; D3 = Input[3];
  //   D4 = Input[4]; D5 = Input[5]; D6 = Input[6]; D7 = Input[7]; D8 = Input[8]; D9 = Input[9]; D10 = Input[10];
  //   D11 = Input[11]; D12 = Input[12]; D13 = Input[13]; D14 = Input[14]; D15 = Input[15]; Q0 = out_5[0];
  //   Q1 = out_5[1]; Q2 = out_5[2]; Q3 = out_5[3]; Q4 = out_5[4]; Q5 = out_5[5]; Q6 = out_5[6]; Q7 = out_5[7];
  //   Q8 = out_5[8]; Q9 = out_5[9]; Q10 = out_5[10]; Q11 = out_5[11]; Q12 = out_5[12]; Q13 = out_5[13];
  //   Q14 = out_5[14]; Q15 = out_5[15]; RS = Reset; WE = WriteEnable
endmodule

module RegisterFile (
  input  reset,
  input  [2:0] ReadReg1,
  input  clk,
  input  [2:0] ReadReg2,
  input  [2:0] WriteReg,
  input  [15:0] WriteData,
  input  RegWriteEnable,
  output [15:0] ReadData1,
  output [15:0] ReadData2
);

  wire and_1_out, and_2_out, and_3_out, and_4_out, and_5_out, and_6_out, and_7_out, and_8_out, D0, D1, D2,
       D3, D4, D5, D6, D7, r0, r0_prime, r1_prime, r1_t, r2_prime, r2_t, r3, r3_prime, r4, r4_prime, r5,
       r5_prime, r6, r6_prime, r7, r7_prime;
  wire [15:0] TB0, TB1, TB2, TB3, TB4, TB5, TB6, TB7;

  Decoder #(.select(3), .enable("false")) decoder_1 (
    .out0(D0), .out1(D1), .out2(D2), .out3(D3), .out4(D4), .out5(D5), .out6(D6), .out7(D7), .sel(WriteReg));
  and and_1 (and_1_out, D0, 1'b0);
  and and_2 (and_2_out, D1, RegWriteEnable);
  and and_3 (and_3_out, D2, RegWriteEnable);
  and and_4 (and_4_out, D3, RegWriteEnable);
  and and_5 (and_5_out, D5, RegWriteEnable);
  and and_6 (and_6_out, D6, RegWriteEnable);
  and and_7 (and_7_out, D7, RegWriteEnable);
  and and_8 (and_8_out, D4, RegWriteEnable);
  Register register_1 (.Input(WriteData), .Clk(clk), .WriteEnable(and_1_out), .Reset(reset), .out_5(TB0));
  Register register_2 (.Input(WriteData), .Clk(clk), .WriteEnable(and_2_out), .Reset(reset), .out_5(TB1));
  Register register_3 (.Input(WriteData), .Clk(clk), .WriteEnable(and_3_out), .Reset(reset), .out_5(TB2));
  Register register_4 (.Input(WriteData), .Clk(clk), .WriteEnable(and_4_out), .Reset(reset), .out_5(TB3));
  Register register_5 (.Input(WriteData), .Clk(clk), .WriteEnable(and_8_out), .Reset(reset), .out_5(TB4));
  Register register_6 (.Input(WriteData), .Clk(clk), .WriteEnable(and_5_out), .Reset(reset), .out_5(TB5));
  Register register_7 (.Input(WriteData), .Clk(clk), .WriteEnable(and_6_out), .Reset(reset), .out_5(TB6));
  Register register_8 (.Input(WriteData), .Clk(clk), .WriteEnable(and_7_out), .Reset(reset), .out_5(TB7));
  // Probe on TB0
  // Probe on TB1
  // Probe on TB2
  // Probe on TB3
  // Probe on TB4
  // Probe on TB5
  // Probe on TB6
  // Probe on TB7
  assign ReadData1 = r0 ? TB0 : 16'bz;  // Controlled_Buffer controlled_buffer_1
  assign ReadData1 = r1_t ? TB1 : 16'bz;  // Controlled_Buffer controlled_buffer_2
  assign ReadData1 = r2_t ? TB2 : 16'bz;  // Controlled_Buffer controlled_buffer_3
  assign ReadData1 = r3 ? TB3 : 16'bz;  // Controlled_Buffer controlled_buffer_4
  assign ReadData1 = r4 ? TB4 : 16'bz;  // Controlled_Buffer controlled_buffer_5
  assign ReadData1 = r5 ? TB5 : 16'bz;  // Controlled_Buffer controlled_buffer_6
  assign ReadData1 = r6 ? TB6 : 16'bz;  // Controlled_Buffer controlled_buffer_7
  assign ReadData1 = r7 ? TB7 : 16'bz;  // Controlled_Buffer controlled_buffer_8
  assign ReadData2 = r0_prime ? TB0 : 16'bz;  // Controlled_Buffer controlled_buffer_9
  assign ReadData2 = r1_prime ? TB1 : 16'bz;  // Controlled_Buffer controlled_buffer_10
  assign ReadData2 = r2_prime ? TB2 : 16'bz;  // Controlled_Buffer controlled_buffer_11
  assign ReadData2 = r3_prime ? TB3 : 16'bz;  // Controlled_Buffer controlled_buffer_12
  assign ReadData2 = r4_prime ? TB4 : 16'bz;  // Controlled_Buffer controlled_buffer_13
  assign ReadData2 = r5_prime ? TB5 : 16'bz;  // Controlled_Buffer controlled_buffer_14
  assign ReadData2 = r6_prime ? TB6 : 16'bz;  // Controlled_Buffer controlled_buffer_15
  assign ReadData2 = r7_prime ? TB7 : 16'bz;  // Controlled_Buffer controlled_buffer_16
  Decoder #(.select(3), .enable("false")) decoder_2 (
    .out0(r0), .out1(r1_t), .out2(r2_t), .out3(r3), .out4(r4), .out5(r5), .out6(r6), .out7(r7), .sel(ReadReg1));
  Decoder #(.select(3), .enable("false")) decoder_3 (
    .out0(r0_prime), .out1(r1_prime), .out2(r2_prime), .out3(r3_prime), .out4(r4_prime), .out5(r5_prime),
    .out6(r6_prime), .out7(r7_prime), .sel(ReadReg2));

  // Other names for the same wires on the sheet: data[15:0] = WriteData; R1[2:0] = ReadReg1; R2[2:0] = ReadReg2;
  //   TB0_prime[15:0] = TB0; TB1_prime[15:0] = TB1; TB2_prime[15:0] = TB2; TB3_prime[15:0] = TB3;
  //   TB4_prime[15:0] = TB4; TB5_prime[15:0] = TB5; TB6_prime[15:0] = TB6; TB7_prime[15:0] = TB7; WE = RegWriteEnable
endmodule

module _1_Bit_Full_Adder (
  input  Cin,
  input  A,
  input  B,
  output Sum,
  output Cout
);

  wire A_B_out, and_1_out, xor_1_out;

  xor xor_1 (xor_1_out, A, B);
  and A_B (A_B_out, B, A);
  xor xor_2 (Cout, and_1_out, A_B_out);
  xor xor_3 (Sum, Cin, xor_1_out);
  and and_1 (and_1_out, xor_1_out, Cin);
endmodule

module _16_Bit_Ripple_Adder (
  input  [15:0] A,
  input  sub,
  input  [15:0] B,
  output [15:0] result,
  output ovf
);

  wire C0, C1, C2, C3, C4, C5, C6, C7, C8, C9, C10, C11, C12, C13, C14, C15, cin, cout,
       n1_bit_full_adder_1_cout, n1_bit_full_adder_2_cout, n1_bit_full_adder_3_cout,
       n1_bit_full_adder_4_cout, n1_bit_full_adder_5_cout, n1_bit_full_adder_6_cout,
       n1_bit_full_adder_7_cout, n1_bit_full_adder_8_cout, n1_bit_full_adder_9_cout,
       n1_bit_full_adder_10_cout, n1_bit_full_adder_11_cout, n1_bit_full_adder_12_cout,
       n1_bit_full_adder_13_cout, n1_bit_full_adder_14_cout;

  _1_Bit_Full_Adder u_1_bit_full_adder_1 (
    .Cin(sub), .A(A[0]), .B(C0), .Sum(result[0]), .Cout(n1_bit_full_adder_1_cout));
  _1_Bit_Full_Adder u_1_bit_full_adder_2 (
    .Cin(n1_bit_full_adder_1_cout), .A(A[1]), .B(C1), .Sum(result[1]), .Cout(n1_bit_full_adder_2_cout));
  _1_Bit_Full_Adder u_1_bit_full_adder_3 (
    .Cin(n1_bit_full_adder_2_cout), .A(A[2]), .B(C2), .Sum(result[2]), .Cout(n1_bit_full_adder_3_cout));
  _1_Bit_Full_Adder u_1_bit_full_adder_4 (
    .Cin(n1_bit_full_adder_3_cout), .A(A[3]), .B(C3), .Sum(result[3]), .Cout(n1_bit_full_adder_4_cout));
  _1_Bit_Full_Adder u_1_bit_full_adder_5 (
    .Cin(n1_bit_full_adder_4_cout), .A(A[4]), .B(C4), .Sum(result[4]), .Cout(n1_bit_full_adder_5_cout));
  _1_Bit_Full_Adder u_1_bit_full_adder_6 (
    .Cin(n1_bit_full_adder_5_cout), .A(A[5]), .B(C5), .Sum(result[5]), .Cout(n1_bit_full_adder_6_cout));
  _1_Bit_Full_Adder u_1_bit_full_adder_7 (
    .Cin(n1_bit_full_adder_6_cout), .A(A[6]), .B(C6), .Sum(result[6]), .Cout(n1_bit_full_adder_7_cout));
  _1_Bit_Full_Adder u_1_bit_full_adder_8 (
    .Cin(n1_bit_full_adder_7_cout), .A(A[7]), .B(C7), .Sum(result[7]), .Cout(n1_bit_full_adder_8_cout));
  _1_Bit_Full_Adder u_1_bit_full_adder_9 (
    .Cin(n1_bit_full_adder_8_cout), .A(A[8]), .B(C8), .Sum(result[8]), .Cout(n1_bit_full_adder_9_cout));
  _1_Bit_Full_Adder u_1_bit_full_adder_10 (
    .Cin(n1_bit_full_adder_9_cout), .A(A[9]), .B(C9), .Sum(result[9]), .Cout(n1_bit_full_adder_10_cout));
  _1_Bit_Full_Adder u_1_bit_full_adder_11 (
    .Cin(n1_bit_full_adder_10_cout), .A(A[10]), .B(C10), .Sum(result[10]), .Cout(n1_bit_full_adder_11_cout));
  _1_Bit_Full_Adder u_1_bit_full_adder_12 (
    .Cin(n1_bit_full_adder_11_cout), .A(A[11]), .B(C11), .Sum(result[11]), .Cout(n1_bit_full_adder_12_cout));
  _1_Bit_Full_Adder u_1_bit_full_adder_13 (
    .Cin(n1_bit_full_adder_12_cout), .A(A[12]), .B(C12), .Sum(result[12]), .Cout(n1_bit_full_adder_13_cout));
  _1_Bit_Full_Adder u_1_bit_full_adder_14 (
    .Cin(n1_bit_full_adder_13_cout), .A(A[13]), .B(C13), .Sum(result[13]), .Cout(n1_bit_full_adder_14_cout));
  _1_Bit_Full_Adder u_1_bit_full_adder_15 (
    .Cin(n1_bit_full_adder_14_cout), .A(A[14]), .B(C14), .Sum(result[14]), .Cout(cin));
  _1_Bit_Full_Adder u_1_bit_full_adder_16 (.Cin(cin), .A(A[15]), .B(C15), .Sum(result[15]), .Cout(cout));
  xor XOR (C0, sub, B[0]);
  xor XOR_2 (C4, sub, B[4]);
  xor XOR_3 (C8, sub, B[8]);
  xor XOR_4 (C12, sub, B[12]);
  xor XOR_5 (C1, sub, B[1]);
  xor XOR_6 (C5, sub, B[5]);
  xor XOR_7 (C9, sub, B[9]);
  xor XOR_8 (C13, sub, B[13]);
  xor XOR_9 (C2, sub, B[2]);
  xor XOR_10 (C6, sub, B[6]);
  xor XOR_11 (C10, sub, B[10]);
  xor XOR_12 (C14, sub, B[14]);
  xor XOR_13 (C3, sub, B[3]);
  xor XOR_14 (C7, sub, B[7]);
  xor XOR_15 (C11, sub, B[11]);
  xor XOR_16 (C15, sub, B[15]);
  xor XOR_17 (ovf, cout, cin);

  // Other names for the same wires on the sheet: S0 = result[0]; S1 = result[1]; S2 = result[2]; S3 = result[3];
  //   S4 = result[4]; S5 = result[5]; S6 = result[6]; S7 = result[7]; S8 = result[8]; S9 = result[9];
  //   S10 = result[10]; S11 = result[11]; S12 = result[12]; S13 = result[13]; S14 = result[14]; S15 = result[15]
endmodule

module _6_16_Sign_Extender (
  input  [5:0] Input,
  output [15:0] out
);


  assign out = {{11{Input[5]}}, Input[4:0]};
endmodule

module _12_16_Sign_Extender (
  input  [11:0] Input,
  output [15:0] out
);


  assign out = {{5{Input[11]}}, Input[10:0]};
endmodule

module Left_Shifter (
  input  [15:0] \input ,
  input  [2:0] shamt,
  output [15:0] \output 
);

  wire multiplexer_1_out, multiplexer_2_out, multiplexer_3_out, multiplexer_4_out, multiplexer_5_out,
       multiplexer_6_out, multiplexer_7_out, multiplexer_8_out, multiplexer_9_out, multiplexer_10_out,
       multiplexer_11_out, multiplexer_12_out, multiplexer_13_out, multiplexer_14_out, multiplexer_15_out,
       multiplexer_16_out, multiplexer_17_out, multiplexer_18_out, multiplexer_21_out, multiplexer_22_out,
       multiplexer_23_out, multiplexer_24_out, multiplexer_28_out, multiplexer_29_out, multiplexer_30_out,
       multiplexer_31_out, multiplexer_32_out, multiplexer_33_out, multiplexer_36_out, multiplexer_37_out,
       multiplexer_38_out, multiplexer_42_out;

  Multiplexer #(.enable("false")) multiplexer_1 (
    .in0(\input [15]), .in1(\input [14]), .out(multiplexer_1_out), .sel(shamt[0]));
  Multiplexer #(.enable("false")) multiplexer_2 (
    .in0(\input [14]), .in1(\input [13]), .out(multiplexer_2_out), .sel(shamt[0]));
  Multiplexer #(.enable("false")) multiplexer_3 (
    .in0(\input [13]), .in1(\input [12]), .out(multiplexer_3_out), .sel(shamt[0]));
  Multiplexer #(.enable("false")) multiplexer_4 (
    .in0(multiplexer_1_out), .in1(multiplexer_3_out), .out(multiplexer_4_out), .sel(shamt[1]));
  Multiplexer #(.enable("false")) multiplexer_5 (
    .in0(\input [12]), .in1(\input [11]), .out(multiplexer_5_out), .sel(shamt[0]));
  Multiplexer #(.enable("false")) multiplexer_6 (
    .in0(\input [11]), .in1(\input [10]), .out(multiplexer_6_out), .sel(shamt[0]));
  Multiplexer #(.enable("false")) multiplexer_7 (
    .in0(multiplexer_2_out), .in1(multiplexer_5_out), .out(multiplexer_7_out), .sel(shamt[1]));
  Multiplexer #(.enable("false")) multiplexer_8 (
    .in0(multiplexer_3_out), .in1(multiplexer_6_out), .out(multiplexer_8_out), .sel(shamt[1]));
  Multiplexer #(.enable("false")) multiplexer_9 (
    .in0(multiplexer_5_out), .in1(multiplexer_10_out), .out(multiplexer_9_out), .sel(shamt[1]));
  Multiplexer #(.enable("false")) multiplexer_10 (
    .in0(\input [10]), .in1(\input [9]), .out(multiplexer_10_out), .sel(shamt[0]));
  Multiplexer #(.enable("false")) multiplexer_11 (
    .in0(\input [9]), .in1(\input [8]), .out(multiplexer_11_out), .sel(shamt[0]));
  Multiplexer #(.enable("false")) multiplexer_12 (
    .in0(\input [8]), .in1(\input [7]), .out(multiplexer_12_out), .sel(shamt[0]));
  Multiplexer #(.enable("false")) multiplexer_13 (
    .in0(multiplexer_6_out), .in1(multiplexer_11_out), .out(multiplexer_13_out), .sel(shamt[1]));
  Multiplexer #(.enable("false")) multiplexer_14 (
    .in0(multiplexer_10_out), .in1(multiplexer_12_out), .out(multiplexer_14_out), .sel(shamt[1]));
  Multiplexer #(.enable("false")) multiplexer_15 (
    .in0(multiplexer_11_out), .in1(multiplexer_16_out), .out(multiplexer_15_out), .sel(shamt[1]));
  Multiplexer #(.enable("false")) multiplexer_16 (
    .in0(\input [7]), .in1(\input [6]), .out(multiplexer_16_out), .sel(shamt[0]));
  Multiplexer #(.enable("false")) multiplexer_17 (
    .in0(\input [6]), .in1(\input [5]), .out(multiplexer_17_out), .sel(shamt[0]));
  Multiplexer #(.enable("false")) multiplexer_18 (
    .in0(\input [5]), .in1(\input [4]), .out(multiplexer_18_out), .sel(shamt[0]));
  Multiplexer #(.enable("false")) multiplexer_19 (
    .in0(multiplexer_4_out), .in1(multiplexer_13_out), .out(\output [15]), .sel(shamt[2]));
  Multiplexer #(.enable("false")) multiplexer_20 (
    .in0(multiplexer_7_out), .in1(multiplexer_14_out), .out(\output [14]), .sel(shamt[2]));
  Multiplexer #(.enable("false")) multiplexer_21 (
    .in0(multiplexer_12_out), .in1(multiplexer_17_out), .out(multiplexer_21_out), .sel(shamt[1]));
  Multiplexer #(.enable("false")) multiplexer_22 (
    .in0(multiplexer_16_out), .in1(multiplexer_18_out), .out(multiplexer_22_out), .sel(shamt[1]));
  Multiplexer #(.enable("false")) multiplexer_23 (
    .in0(\input [4]), .in1(\input [3]), .out(multiplexer_23_out), .sel(shamt[0]));
  Multiplexer #(.enable("false")) multiplexer_24 (
    .in0(\input [3]), .in1(\input [2]), .out(multiplexer_24_out), .sel(shamt[0]));
  Multiplexer #(.enable("false")) multiplexer_25 (
    .in0(multiplexer_8_out), .in1(multiplexer_15_out), .out(\output [13]), .sel(shamt[2]));
  Multiplexer #(.enable("false")) multiplexer_26 (
    .in0(multiplexer_9_out), .in1(multiplexer_21_out), .out(\output [12]), .sel(shamt[2]));
  Multiplexer #(.enable("false")) multiplexer_27 (
    .in0(multiplexer_13_out), .in1(multiplexer_22_out), .out(\output [11]), .sel(shamt[2]));
  Multiplexer #(.enable("false")) multiplexer_28 (
    .in0(multiplexer_17_out), .in1(multiplexer_23_out), .out(multiplexer_28_out), .sel(shamt[1]));
  Multiplexer #(.enable("false")) multiplexer_29 (
    .in0(multiplexer_18_out), .in1(multiplexer_24_out), .out(multiplexer_29_out), .sel(shamt[1]));
  Multiplexer #(.enable("false")) multiplexer_30 (
    .in0(multiplexer_23_out), .in1(multiplexer_31_out), .out(multiplexer_30_out), .sel(shamt[1]));
  Multiplexer #(.enable("false")) multiplexer_31 (
    .in0(\input [2]), .in1(\input [1]), .out(multiplexer_31_out), .sel(shamt[0]));
  Multiplexer #(.enable("false")) multiplexer_32 (
    .in0(\input [1]), .in1(\input [0]), .out(multiplexer_32_out), .sel(shamt[0]));
  Multiplexer #(.enable("false")) multiplexer_33 (
    .in0(\input [0]), .in1(1'b0), .out(multiplexer_33_out), .sel(shamt[0]));
  Multiplexer #(.enable("false")) multiplexer_34 (
    .in0(multiplexer_14_out), .in1(multiplexer_28_out), .out(\output [10]), .sel(shamt[2]));
  Multiplexer #(.enable("false")) multiplexer_35 (
    .in0(multiplexer_15_out), .in1(multiplexer_29_out), .out(\output [9]), .sel(shamt[2]));
  Multiplexer #(.enable("false")) multiplexer_36 (
    .in0(multiplexer_24_out), .in1(multiplexer_32_out), .out(multiplexer_36_out), .sel(shamt[1]));
  Multiplexer #(.enable("false")) multiplexer_37 (
    .in0(multiplexer_31_out), .in1(multiplexer_33_out), .out(multiplexer_37_out), .sel(shamt[1]));
  Multiplexer #(.enable("false")) multiplexer_38 (
    .in0(multiplexer_32_out), .in1(1'b0), .out(multiplexer_38_out), .sel(shamt[1]));
  Multiplexer #(.enable("false")) multiplexer_39 (
    .in0(multiplexer_21_out), .in1(multiplexer_30_out), .out(\output [8]), .sel(shamt[2]));
  Multiplexer #(.enable("false")) multiplexer_40 (
    .in0(multiplexer_22_out), .in1(multiplexer_36_out), .out(\output [7]), .sel(shamt[2]));
  Multiplexer #(.enable("false")) multiplexer_41 (
    .in0(multiplexer_28_out), .in1(multiplexer_37_out), .out(\output [6]), .sel(shamt[2]));
  Multiplexer #(.enable("false")) multiplexer_42 (
    .in0(multiplexer_33_out), .in1(1'b0), .out(multiplexer_42_out), .sel(shamt[1]));
  Multiplexer #(.enable("false")) multiplexer_43 (
    .in0(multiplexer_29_out), .in1(multiplexer_38_out), .out(\output [5]), .sel(shamt[2]));
  Multiplexer #(.enable("false")) multiplexer_44 (
    .in0(multiplexer_30_out), .in1(multiplexer_42_out), .out(\output [4]), .sel(shamt[2]));
  Multiplexer #(.enable("false")) multiplexer_45 (
    .in0(multiplexer_36_out), .in1(1'b0), .out(\output [3]), .sel(shamt[2]));
  Multiplexer #(.enable("false")) multiplexer_46 (
    .in0(multiplexer_37_out), .in1(1'b0), .out(\output [2]), .sel(shamt[2]));
  Multiplexer #(.enable("false")) multiplexer_47 (
    .in0(multiplexer_38_out), .in1(1'b0), .out(\output [1]), .sel(shamt[2]));
  Multiplexer #(.enable("false")) multiplexer_48 (
    .in0(multiplexer_42_out), .in1(1'b0), .out(\output [0]), .sel(shamt[2]));

  // Other names for the same wires on the sheet: _0 = shamt[0]; _1 = shamt[1]; _2 = shamt[2]
endmodule

module Right_Shifter (
  input  [15:0] \input ,
  input  [2:0] shamt,
  output [15:0] \output 
);

  wire multiplexer_1_out, multiplexer_2_out, multiplexer_3_out, multiplexer_4_out, multiplexer_5_out,
       multiplexer_6_out, multiplexer_7_out, multiplexer_8_out, multiplexer_9_out, multiplexer_10_out,
       multiplexer_11_out, multiplexer_12_out, multiplexer_13_out, multiplexer_14_out, multiplexer_15_out,
       multiplexer_16_out, multiplexer_17_out, multiplexer_18_out, multiplexer_21_out, multiplexer_22_out,
       multiplexer_23_out, multiplexer_24_out, multiplexer_28_out, multiplexer_29_out, multiplexer_30_out,
       multiplexer_31_out, multiplexer_32_out, multiplexer_33_out, multiplexer_36_out, multiplexer_37_out,
       multiplexer_38_out, multiplexer_42_out;

  Multiplexer #(.enable("false")) multiplexer_1 (
    .in0(\input [0]), .in1(\input [1]), .out(multiplexer_1_out), .sel(shamt[0]));
  Multiplexer #(.enable("false")) multiplexer_2 (
    .in0(\input [1]), .in1(\input [2]), .out(multiplexer_2_out), .sel(shamt[0]));
  Multiplexer #(.enable("false")) multiplexer_3 (
    .in0(\input [2]), .in1(\input [3]), .out(multiplexer_3_out), .sel(shamt[0]));
  Multiplexer #(.enable("false")) multiplexer_4 (
    .in0(multiplexer_1_out), .in1(multiplexer_3_out), .out(multiplexer_4_out), .sel(shamt[1]));
  Multiplexer #(.enable("false")) multiplexer_5 (
    .in0(\input [3]), .in1(\input [4]), .out(multiplexer_5_out), .sel(shamt[0]));
  Multiplexer #(.enable("false")) multiplexer_6 (
    .in0(\input [4]), .in1(\input [5]), .out(multiplexer_6_out), .sel(shamt[0]));
  Multiplexer #(.enable("false")) multiplexer_7 (
    .in0(multiplexer_2_out), .in1(multiplexer_5_out), .out(multiplexer_7_out), .sel(shamt[1]));
  Multiplexer #(.enable("false")) multiplexer_8 (
    .in0(multiplexer_3_out), .in1(multiplexer_6_out), .out(multiplexer_8_out), .sel(shamt[1]));
  Multiplexer #(.enable("false")) multiplexer_9 (
    .in0(multiplexer_5_out), .in1(multiplexer_10_out), .out(multiplexer_9_out), .sel(shamt[1]));
  Multiplexer #(.enable("false")) multiplexer_10 (
    .in0(\input [5]), .in1(\input [6]), .out(multiplexer_10_out), .sel(shamt[0]));
  Multiplexer #(.enable("false")) multiplexer_11 (
    .in0(\input [6]), .in1(\input [7]), .out(multiplexer_11_out), .sel(shamt[0]));
  Multiplexer #(.enable("false")) multiplexer_12 (
    .in0(\input [7]), .in1(\input [8]), .out(multiplexer_12_out), .sel(shamt[0]));
  Multiplexer #(.enable("false")) multiplexer_13 (
    .in0(multiplexer_6_out), .in1(multiplexer_11_out), .out(multiplexer_13_out), .sel(shamt[1]));
  Multiplexer #(.enable("false")) multiplexer_14 (
    .in0(multiplexer_10_out), .in1(multiplexer_12_out), .out(multiplexer_14_out), .sel(shamt[1]));
  Multiplexer #(.enable("false")) multiplexer_15 (
    .in0(multiplexer_11_out), .in1(multiplexer_16_out), .out(multiplexer_15_out), .sel(shamt[1]));
  Multiplexer #(.enable("false")) multiplexer_16 (
    .in0(\input [8]), .in1(\input [9]), .out(multiplexer_16_out), .sel(shamt[0]));
  Multiplexer #(.enable("false")) multiplexer_17 (
    .in0(\input [9]), .in1(\input [10]), .out(multiplexer_17_out), .sel(shamt[0]));
  Multiplexer #(.enable("false")) multiplexer_18 (
    .in0(\input [10]), .in1(\input [11]), .out(multiplexer_18_out), .sel(shamt[0]));
  Multiplexer #(.enable("false")) multiplexer_19 (
    .in0(multiplexer_4_out), .in1(multiplexer_13_out), .out(\output [0]), .sel(shamt[2]));
  Multiplexer #(.enable("false")) multiplexer_20 (
    .in0(multiplexer_7_out), .in1(multiplexer_14_out), .out(\output [1]), .sel(shamt[2]));
  Multiplexer #(.enable("false")) multiplexer_21 (
    .in0(multiplexer_12_out), .in1(multiplexer_17_out), .out(multiplexer_21_out), .sel(shamt[1]));
  Multiplexer #(.enable("false")) multiplexer_22 (
    .in0(multiplexer_16_out), .in1(multiplexer_18_out), .out(multiplexer_22_out), .sel(shamt[1]));
  Multiplexer #(.enable("false")) multiplexer_23 (
    .in0(\input [11]), .in1(\input [12]), .out(multiplexer_23_out), .sel(shamt[0]));
  Multiplexer #(.enable("false")) multiplexer_24 (
    .in0(\input [12]), .in1(\input [13]), .out(multiplexer_24_out), .sel(shamt[0]));
  Multiplexer #(.enable("false")) multiplexer_25 (
    .in0(multiplexer_8_out), .in1(multiplexer_15_out), .out(\output [2]), .sel(shamt[2]));
  Multiplexer #(.enable("false")) multiplexer_26 (
    .in0(multiplexer_9_out), .in1(multiplexer_21_out), .out(\output [3]), .sel(shamt[2]));
  Multiplexer #(.enable("false")) multiplexer_27 (
    .in0(multiplexer_13_out), .in1(multiplexer_22_out), .out(\output [4]), .sel(shamt[2]));
  Multiplexer #(.enable("false")) multiplexer_28 (
    .in0(multiplexer_17_out), .in1(multiplexer_23_out), .out(multiplexer_28_out), .sel(shamt[1]));
  Multiplexer #(.enable("false")) multiplexer_29 (
    .in0(multiplexer_18_out), .in1(multiplexer_24_out), .out(multiplexer_29_out), .sel(shamt[1]));
  Multiplexer #(.enable("false")) multiplexer_30 (
    .in0(multiplexer_23_out), .in1(multiplexer_31_out), .out(multiplexer_30_out), .sel(shamt[1]));
  Multiplexer #(.enable("false")) multiplexer_31 (
    .in0(\input [13]), .in1(\input [14]), .out(multiplexer_31_out), .sel(shamt[0]));
  Multiplexer #(.enable("false")) multiplexer_32 (
    .in0(\input [14]), .in1(\input [15]), .out(multiplexer_32_out), .sel(shamt[0]));
  Multiplexer #(.enable("false")) multiplexer_33 (
    .in0(\input [15]), .in1(1'b0), .out(multiplexer_33_out), .sel(shamt[0]));
  Multiplexer #(.enable("false")) multiplexer_34 (
    .in0(multiplexer_14_out), .in1(multiplexer_28_out), .out(\output [5]), .sel(shamt[2]));
  Multiplexer #(.enable("false")) multiplexer_35 (
    .in0(multiplexer_15_out), .in1(multiplexer_29_out), .out(\output [6]), .sel(shamt[2]));
  Multiplexer #(.enable("false")) multiplexer_36 (
    .in0(multiplexer_24_out), .in1(multiplexer_32_out), .out(multiplexer_36_out), .sel(shamt[1]));
  Multiplexer #(.enable("false")) multiplexer_37 (
    .in0(multiplexer_31_out), .in1(multiplexer_33_out), .out(multiplexer_37_out), .sel(shamt[1]));
  Multiplexer #(.enable("false")) multiplexer_38 (
    .in0(multiplexer_32_out), .in1(1'b0), .out(multiplexer_38_out), .sel(shamt[1]));
  Multiplexer #(.enable("false")) multiplexer_39 (
    .in0(multiplexer_21_out), .in1(multiplexer_30_out), .out(\output [7]), .sel(shamt[2]));
  Multiplexer #(.enable("false")) multiplexer_40 (
    .in0(multiplexer_22_out), .in1(multiplexer_36_out), .out(\output [8]), .sel(shamt[2]));
  Multiplexer #(.enable("false")) multiplexer_41 (
    .in0(multiplexer_28_out), .in1(multiplexer_37_out), .out(\output [9]), .sel(shamt[2]));
  Multiplexer #(.enable("false")) multiplexer_42 (
    .in0(multiplexer_33_out), .in1(1'b0), .out(multiplexer_42_out), .sel(shamt[1]));
  Multiplexer #(.enable("false")) multiplexer_43 (
    .in0(multiplexer_29_out), .in1(multiplexer_38_out), .out(\output [10]), .sel(shamt[2]));
  Multiplexer #(.enable("false")) multiplexer_44 (
    .in0(multiplexer_30_out), .in1(multiplexer_42_out), .out(\output [11]), .sel(shamt[2]));
  Multiplexer #(.enable("false")) multiplexer_45 (
    .in0(multiplexer_36_out), .in1(1'b0), .out(\output [12]), .sel(shamt[2]));
  Multiplexer #(.enable("false")) multiplexer_46 (
    .in0(multiplexer_37_out), .in1(1'b0), .out(\output [13]), .sel(shamt[2]));
  Multiplexer #(.enable("false")) multiplexer_47 (
    .in0(multiplexer_38_out), .in1(1'b0), .out(\output [14]), .sel(shamt[2]));
  Multiplexer #(.enable("false")) multiplexer_48 (
    .in0(multiplexer_42_out), .in1(1'b0), .out(\output [15]), .sel(shamt[2]));

  // Other names for the same wires on the sheet: _0 = shamt[0]; _1 = shamt[1]; _2 = shamt[2]
endmodule
